// Logisim project hw4.circ as structural Verilog: 1 circuit, main circuit main
module main (
  input  A,
  input  B,
  input  C,
  input  D
);

  wire a_nb_nc_2_out, a_nb_nc_out, A_out, B_out, C_out, D_out, E_out, F_out, G_out, na_nb_out, na_nbc_out,
       na_nc_nd_out, nab_nc_out, nab_ncd_out, nab_nd_out, nab_out, nabd_out, nac_nd_out, nac_out, nacd_out,
       nb_nc_nd_out, nb_nc_out, not_1_out, not_2_out, not_3_out, not_4_out;

  not not_1 (not_1_out, A);
  not not_2 (not_2_out, B);
  not not_3 (not_3_out, C);
  not not_4 (not_4_out, D);
  and a_nb_nc (a_nb_nc_out, A, not_2_out, not_3_out);
  and nb_nc_nd (nb_nc_nd_out, not_3_out, not_2_out, not_4_out);
  and nabd (nabd_out, not_1_out, D, B);
  and nac (nac_out, not_1_out, C);
  and na_nb (na_nb_out, not_1_out, not_2_out);
  and nacd (nacd_out, C, not_1_out, D);
  and na_nc_nd (na_nc_nd_out, not_1_out, not_3_out, not_4_out);
  and nb_nc (nb_nc_out, not_2_out, not_3_out);
  and nab (nab_out, not_1_out, B);
  and na_nbc (na_nbc_out, not_1_out, C, not_2_out);
  and nac_nd (nac_nd_out, not_1_out, C, not_4_out);
  and nab_ncd (nab_ncd_out, not_1_out, B, not_3_out, D);
  and nab_nd (nab_nd_out, not_1_out, B, not_4_out);
  and nab_nc (nab_nc_out, not_1_out, B, not_3_out);
  and a_nb_nc_2 (a_nb_nc_2_out, not_3_out, not_2_out, A);
  or u_A (A_out, a_nb_nc_out, nb_nc_nd_out, nabd_out, nac_out);
  or u_B (B_out, nb_nc_out, na_nc_nd_out, nacd_out, na_nb_out);
  or u_C (C_out, nacd_out, nb_nc_out, nab_out);
  or u_D (D_out, nb_nc_nd_out, a_nb_nc_out, na_nbc_out, nac_nd_out, nab_ncd_out);
  or E (E_out, nac_nd_out, nb_nc_nd_out);
  or F (F_out, a_nb_nc_2_out, nab_nc_out, nb_nc_nd_out, nab_nd_out);
  or G (G_out, na_nbc_out, nab_nc_out, a_nb_nc_2_out, nac_nd_out);
  _7_Segment_Display u_7_segment_display_1 (
    .g(G_out), .f(F_out), .a(A_out), .b(B_out), .e(E_out), .d(D_out), .c(C_out));  // open: dp
endmodule
